// Digital circuit cpu.dig as structural Verilog
module cpu (
  input  clk,
  input  fetch_en,
  input  jmp_en
);

  wire decode_1_p4, Decode_Execute_p6, Decode_Execute_p7;
  wire [3:0] decode_1_p5, decode_1_p6;
  wire [15:0] alu_1_p4, decode_1_p3, decode_1_p7, Decode_Execute_p5, IR_q, mem_1_p4, mem_2_q, pc_1_p5,
       RegFile_lhs, RegFile_rhs, res_2_q, res_q;

  Register #(.Bits(16)) IR (.D(decode_1_p3), .C(clk), .Q(IR_q));  // open: en
  // decode decode_1: pin names not known; wires that end beside it: IR_q, clk, decode_1_p3, decode_1_p4, decode_1_p5, decode_1_p6, decode_1_p7
  operands RegFile (
    .ProgCt(pc_1_p5), .RegA(decode_1_p5), .RegB(decode_1_p6), .Imm(decode_1_p7), .clk(clk),
    .DataIn(decode_1_p3), .Lhs(RegFile_lhs), .Rhs(RegFile_rhs));  // open: WrEn
  // de_ex Decode_Execute: pin names not known; wires that end beside it: decode_1_p4, RegFile_lhs, RegFile_rhs, clk, Decode_Execute_p5, Decode_Execute_p6, Decode_Execute_p7
  // alu alu_1: pin names not known; wires that end beside it: Decode_Execute_p5, Decode_Execute_p6, Decode_Execute_p7, alu_1_p4
  // pc pc_1: pin names not known; wires that end beside it: clk, fetch_en, alu_1_p4, jmp_en, pc_1_p5
  D_FF #(.Bits(16)) res (.D(alu_1_p4), .C(clk), .Q(res_q));  // open: nQ
  D_FF #(.Bits(16)) src (.D(Decode_Execute_p5), .C(clk));  // open: Q, nQ
  // mem mem_1: pin names not known; wires that end beside it: res_q, 1'b0, 1'b0, mem_1_p4
  D_FF #(.Bits(16)) mem_2 (.D(mem_1_p4), .C(clk), .Q(mem_2_q));  // open: nQ
  D_FF #(.Bits(16)) res_2 (.D(res_q), .C(clk), .Q(res_2_q));  // open: nQ
  Multiplexer multiplexer_1 (.in_0(mem_2_q[0]), .in_1(res_2_q[0]), .out(decode_1_p3[0]));  // open: sel
  // Pins of 1 and 16 bits meet at mem_2_q
  // Pins of 1 and 16 bits meet at res_2_q
  // Pins of 1 and 16 bits meet at decode_1_p3
endmodule
