// Digital circuit decode.dig as structural Verilog
module decode (
  input  [15:0] Inst,
  input  clk,
  output MemRdEn,
  output [1:0] MemWrEn,
  output [1:0] WrBackEn,
  output [3:0] RegA,
  output [3:0] RegB,
  output [15:0] Imm,
  output [3:0] AluOp,
  output [2:0] JmpCond
);

  wire [31:28] Decoder_d;

  ROM #(.AddrBits(16), .Bits(32)) Decoder (.D({Decoder_d, WrBackEn, MemWrEn, MemRdEn, JmpCond, AluOp, Imm}));  // open: A, sel

  assign RegA = Inst[7:4];
  assign RegB = Inst[3:0];

  // Other names for the same wires on the sheet: b0 = Inst[0]; b1 = Inst[1]; b2 = Inst[2]; b3 = Inst[3]; b4 = Inst[4];
  //   b5 = Inst[5]; b6 = Inst[6]; b7 = Inst[7]; b8 = Inst[8]; b9 = Inst[9]; b10 = Inst[10]; b11 = Inst[11];
  //   b12 = Inst[12]; b13 = Inst[13]; b14 = Inst[14]; b15 = Inst[15]
endmodule
